# Fritzing sketch Circuit (saved by Fritzing 0.8.7b)

parts:
  Часть1 = Arduino Uno (Rev3) - ICSP
  L298N1 = L298N DC motor driver
  BT1 = Bluetooth HC-06u [package=THT]
  U1 = SWITCH_SPDT [package=kps-1290]
  VCC1 = Battery block 9V
  M1 = DC Motor  # not connected
  M2 = DC Motor  # not connected
  J1 = Basic Servo
  C1 = Capacitor [package=cap-pth-small2]  # not connected

nets:
  GND: Часть1.GND, BT1.GND, U1.S, J1.gnd
  N1: Часть1.D0/RX, BT1.TXD
  N2: Часть1.D1/TX, BT1.RXD
  N3: Часть1.D2, L298N1.IN3
  N4: Часть1.D3_PWM, L298N1.ENB
  N5: Часть1.D4, L298N1.IN4
  N6: Часть1.D5_PWM, J1.pulse
  3V3: Часть1.3V3, BT1.VCC
  5V: Часть1.5V, J1.vcc
  VIN: Часть1.VIN, L298N1.12V, VCC1.+

custom parts:
  L298N DC motor driver: 2x DC motor driver with 78M05 positive voltage regulator (7..35 V) L298N: max 46 V, 2 A Set 5 V Enable jumper to enable 5 V regultor (needed for the L298N) and +5 V output at screw terminal or supply external +5 V at screw terminal Set ENA and/or ENB to +5 V to enable motor permanently or supply ENA and/or ENB with PWM signal IN1 and IN2 set rotation directory for motor A (OUT1/OUT2) IN2 and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
  Bluetooth HC-06u: Bluetooth HC-06 - face up, pins down 16.5mm x 37.5mm PCB
